# Fritzing sketch bearaille (saved by Fritzing 0.9.3b)
breadboards: 1

parts:
  S1 = Pushbutton [package="[THT]"]
  S2 = Pushbutton [package="[THT]"]
  S3 = Pushbutton [package="[THT]"]
  S4 = Pushbutton [package="[THT]"]
  S5 = Pushbutton [package="[THT]"]
  S6 = Pushbutton [package="[THT]"]
  S7 = Pushbutton [package="[THT]"]
  Part3 = RedBear-Duo  # not connected
  Part4 = RedBear-Duo

nets (from the breadboard view):
  N1: S1.Pin_1, S1.Pin_2, Part4.D3
  N2: S1.Pin_3, S1.Pin_4, S2.Pin_3, S2.Pin_4, S3.Pin_3, S3.Pin_4, S4.Pin_3, S4.Pin_4, S5.Pin_3, S5.Pin_4, S6.Pin_3, S6.Pin_4, S7.Pin_3, S7.Pin_4, Part4.GND
  N3: S2.Pin_1, S2.Pin_2, Part4.D1
  N4: S3.Pin_1, S3.Pin_2, Part4.D2
  N5: S4.Pin_1, S4.Pin_2, Part4.D4
  N6: S5.Pin_1, S5.Pin_2, Part4.D5
  N7: S6.Pin_1, S6.Pin_2, Part4.D7
  N8: S7.Pin_1, S7.Pin_2, Part4.D0

custom parts:
  RedBear-Duo: Duo is a thumb-size development board made to simplify the building process of Internet of Things (IoT). This part is a modification of the Particle Photon part by Brett Walach,Fabian Althaus
